# Fritzing sketch arduino-power_amp-rgb_led_strip (saved by Fritzing 0.9.3b)
breadboards: 1

parts:
  Part1 = Arduino Uno (Rev3)
  R1 = Resistor [tolerance=±5% resistance=1k package=THT]
  R2 = Resistor [tolerance=±5% resistance=1k package=THT]
  R3 = Resistor [tolerance=±5% resistance=1k package=THT]
  Q2 = npn-Powertransistor [part_number=TIP31C package="TO220 [THT]"]
  Power_plug1 = Power plug
  Q3 = npn-Powertransistor [part_number=TIP31C package="TO220 [THT]"]
  Q4 = npn-Powertransistor [part_number=TIP31C package="TO220 [THT]"]
  J1 = female pin header, 4 pins [form="♀ (female)"]

nets:
  N1: Part1.D9_PWM, R2.Pin_1
  N2: Part1.D10_PWM/SS, R1.Pin_1
  N3: Part1.D11_PWM/MOSI, R3.Pin_1
  N4: Part1.AREF, Q2.emitter, Power_plug1.GND, Q3.emitter, Q4.emitter
  N5: R1.Pin_0, Q3.base
  N6: R2.Pin_0, Q4.base
  N7: R3.Pin_0, Q2.base
  N8: Q2.collector, J1.pin1
  N9: Power_plug1.VCC, J1.pin4
  N10: Q3.collector, J1.pin2
  N11: Q4.collector, J1.pin3
